# Fritzing sketch paste_dispenser (saved by Fritzing 0.9.3b)
circuit board: 5cm x 4.75cm
breadboards: 1

parts:
  SPARKFUN_PRO_MINI = Arduino Pro Mini v13
  OLED = OLED 0.91" 128x32 I2C SSD1306 (GND/VCC)
  PUSH = Pushbutton [package="[THT]"]
  FASTER = Pushbutton [package="[THT]"]
  SLOWER = Pushbutton [package="[THT]"]
  Serial_to_USB = FTDI Basic Programmer
  TB6612FNG = Adafruit TB6612 DC and Stepper Motor Driver [part_number="Adafruit #2448"]
  MOTOR = Adafruit Gear-Reduced Stepper Motor (small)
  PULL = Pushbutton [package="[THT]"]
  FOOTSWITCH = 2.5mm Audio Jack [package=stereojack2.5mm_stereojack2.5mm]
  STEPPER = screw terminal, 5 pins

nets:
  N1: SPARKFUN_PRO_MINI.DTR, Serial_to_USB.DTR
  N2: SPARKFUN_PRO_MINI.D0/TX, Serial_to_USB.RXI
  N3: SPARKFUN_PRO_MINI.D1/RX, Serial_to_USB.TXO
  VCC: SPARKFUN_PRO_MINI.VCC, OLED.VCC, Serial_to_USB.POWER, TB6612FNG.PWRIN, TB6612FNG.VCC
  GND: SPARKFUN_PRO_MINI.GND, OLED.GND, PUSH.Pin_3, PUSH.Pin_4, FASTER.Pin_3, FASTER.Pin_4, SLOWER.Pin_3, SLOWER.Pin_4, Serial_to_USB.CTS, Serial_to_USB.GND, TB6612FNG.GND, MOTOR.RED, PULL.Pin_3, PULL.Pin_4, FOOTSWITCH.SLEEVE, STEPPER.pin3
  N4: SPARKFUN_PRO_MINI.A4, OLED.SCA
  N5: SPARKFUN_PRO_MINI.A5, OLED.SCL
  N6: SPARKFUN_PRO_MINI.A3, TB6612FNG.AIN1
  N7: SPARKFUN_PRO_MINI.A2, TB6612FNG.AIN2
  N8: SPARKFUN_PRO_MINI.A1, TB6612FNG.BIN1
  N9: SPARKFUN_PRO_MINI.A0, TB6612FNG.BIN2
  N10: SPARKFUN_PRO_MINI.D10_PWM/SS, TB6612FNG.PWMB
  N11: SPARKFUN_PRO_MINI.D9_PWM, TB6612FNG.PWMA
  N12: SPARKFUN_PRO_MINI.D8, TB6612FNG.STBY
  N13: SPARKFUN_PRO_MINI.D7, PULL.Pin_1, PULL.Pin_2
  N14: SPARKFUN_PRO_MINI.D6_PWM, PUSH.Pin_1, PUSH.Pin_2
  N15: SPARKFUN_PRO_MINI.D5_PWM, FASTER.Pin_1, FASTER.Pin_2
  N16: SPARKFUN_PRO_MINI.D4, SLOWER.Pin_1, SLOWER.Pin_2
  N17: SPARKFUN_PRO_MINI.D2, FOOTSWITCH.LEFT, FOOTSWITCH.RIGHT
  N18: TB6612FNG.MOTORA1, MOTOR.BLUE, STEPPER.pin5
  N19: TB6612FNG.MOTORA2, MOTOR.YELLOW, STEPPER.pin4
  N20: TB6612FNG.MOTORB2, MOTOR.PINK, STEPPER.pin2
  N21: TB6612FNG.MOTORB1, MOTOR.ORANGE, STEPPER.pin1

notes:
  Pushbuttons:
  Pull Push Fast Slow Footswitch
  Solder Paste Dispenser w/
  LED on pin 13.
  In sketch:
  breathingled.cpp:
  #define LED_PWM 0
  pins.h:
  kLedPin = 13
  kFootswitchPin = 2;
  kForwardButtonPin = 6;
  kBackwardButtonPin = 7;
  kFastButtonPin = 5;
  kSlowButtonPin = 4;

custom parts:
  OLED 0.91" 128x32 I2C SSD1306 (GND/VCC): OLED 0.91" 128x32 I2C SSD1306 Pinout: GND/VCC/SCL/SDA
  Adafruit TB6612 DC and Stepper Motor Driver: Spin two DC motors, step one bi-polar or uni-polar stepper, or fire off two solenoids with 1.2A per channel using the TB6612. These are perhaps better known as "the drivers in our assembled Adafruit Motorshield or Motor HAT." We really like these dual H-bridges, so if you want to control motors without a shield or HAT these are easy to include on any solderless breadboard or perma-proto.
  Adafruit Gear-Reduced Stepper Motor (small): Adafruit gear-reduction stepper motor (small)
